# Fritzing sketch brielle circuit (saved by Fritzing 0.9.3b)
breadboards: 2

parts:
  S1 = Pushbutton [package="[THT]"]
  S2 = Pushbutton [package="[THT]"]
  S3 = Pushbutton [package="[THT]"]
  S4 = Pushbutton [package="[THT]"]
  S5 = Pushbutton [package="[THT]"]
  S6 = Pushbutton [package="[THT]"]
  S7 = Pushbutton [package="[THT]"]
  S8 = Pushbutton [package="[THT]"]
  Part2 = RedBear Duo

nets:
  N1: S1.Pin_1, S2.Pin_1, S2.Pin_2, S3.Pin_1, S3.Pin_2, S4.Pin_1, S5.Pin_1, S6.Pin_1, S7.Pin_1, S7.Pin_2, S8.Pin_1, S8.Pin_2, Part2.3V3
  N2: S1.Pin_3, S1.Pin_4, Part2.DAC
  N3: S2.Pin_3, S2.Pin_4, Part2.WKP
  N4: S3.Pin_3, S3.Pin_4, Part2.A5
  N5: S4.Pin_3, S4.Pin_4, Part2.A2
  N6: S5.Pin_3, S5.Pin_4, Part2.D7
  N7: S6.Pin_3, S6.Pin_4, Part2.D4
  N8: S7.Pin_3, S7.Pin_4, Part2.D5
  N9: S8.Pin_3, S8.Pin_4, Part2.D6

custom parts:
  RedBear Duo: Duo is a thumb-size development board made to simplify the building process of Internet of Things (IoT). This part is a modification of the Particle Photon part by Brett Walach,Fabian Althaus
